// Logisim project ex01.circ as structural Verilog: 1 circuit, main circuit main
module main (
  input  in_1,
  input  in_2,
  output out_3,
  output out_4,
  output out_5
);

  wire and_2_out, and_3_out, not_1_out, not_2_out;

  not not_1 (not_1_out, in_2);
  not not_2 (not_2_out, in_1);
  and and_1 (out_4, in_1, in_2);
  xnor xnor_1 (out_5, in_1, in_2);
  and and_2 (and_2_out, in_2, not_2_out);
  and and_3 (and_3_out, not_1_out, in_1);
  or or_1 (out_3, and_2_out, and_3_out);
endmodule
