// Logisim project ex02.circ as structural Verilog: 1 circuit, main circuit main
module main (
  input  A0,
  input  A1,
  input  B0,
  input  B1,
  output E,
  output G,
  output L
);

  wire and_2_out, and_3_out, and_4_out, and_5_out, and_6_out, and_7_out, and_8_out, not_1_out, not_2_out,
       not_3_out, not_4_out, not_5_out, not_6_out, not_7_out, not_8_out, not_9_out, xnor_1_out, xnor_2_out,
       xnor_3_out;

  xnor xnor_1 (xnor_1_out, A1, B1);
  xnor xnor_2 (xnor_2_out, A0, B0);
  not not_1 (not_1_out, B0);
  not not_2 (not_2_out, B1);
  not not_3 (not_3_out, A0);
  not not_4 (not_4_out, B1);
  not not_5 (not_5_out, A0);
  not not_6 (not_6_out, A0);
  not not_7 (not_7_out, A1);
  not not_8 (not_8_out, B0);
  not not_9 (not_9_out, A1);
  and and_1 (E, xnor_1_out, xnor_2_out);
  and and_2 (and_2_out, not_1_out, A0);
  xnor xnor_3 (xnor_3_out, B1, A1);
  and and_3 (and_3_out, not_2_out, A1);
  and and_4 (and_4_out, not_3_out, B0, not_4_out);
  and and_5 (and_5_out, B0, not_5_out, A1);
  and and_6 (and_6_out, not_6_out, not_7_out, not_8_out, B1);
  and and_7 (and_7_out, not_9_out, A0, B0, B1);
  and and_8 (and_8_out, and_2_out, xnor_3_out);
  or or_1 (G, and_8_out, and_3_out);
  or or_2 (L, and_4_out, and_5_out, and_6_out, and_7_out);
endmodule
