// Logisim project ex03.circ as structural Verilog: 1 circuit, main circuit main
module main (
  input  D3,
  input  D2,
  input  D1,
  input  D0,
  output P
);

  wire xor_1_out, xor_2_out;

  xor xor_1 (xor_1_out, D3, D2);
  xor xor_2 (xor_2_out, D1, D0);
  xor xor_3 (P, xor_1_out, xor_2_out);
endmodule
