// Logisim project ex04.circ as structural Verilog: 1 circuit, main circuit main
module main (
  input  D3,
  input  D2,
  input  D1,
  input  D0,
  input  P,
  output E
);

  wire xor_1_out, xor_2_out, xor_3_out;

  xor xor_1 (xor_1_out, D3, D2);
  xor xor_2 (xor_2_out, D1, D0);
  xor xor_3 (xor_3_out, xor_1_out, xor_2_out);
  xor xor_4 (E, xor_3_out, P);
endmodule
