// Logisim project ex05.circ as structural Verilog: 1 circuit, main circuit main
module main (
  input  S1,
  input  S2,
  input  S3,
  output V,
  output E
);

  wire and_1_out, and_2_out, and_3_out, xor_1_out, xor_2_out;

  and and_1 (and_1_out, S1, S2);
  and and_2 (and_2_out, S3, S1);
  and and_3 (and_3_out, S2, S3);
  xor xor_1 (xor_1_out, S1, S2);
  xor xor_2 (xor_2_out, S2, S3);
  or or_1 (E, xor_1_out, xor_2_out);
  or or_2 (V, and_1_out, and_2_out, and_3_out);
endmodule
