// Logisim project ex06.circ as structural Verilog: 1 circuit, main circuit main
module main (
  input  R0,
  input  R1,
  input  R2,
  input  R3,
  output G1,
  output G0
);

  wire and_1_out, and_2_out, and_3_out, and_4_out, not_1_out, not_2_out, not_3_out, not_4_out, not_5_out,
       not_6_out, not_7_out;

  not not_1 (not_1_out, R0);
  not not_2 (not_2_out, R0);
  not not_3 (not_3_out, R2);
  not not_4 (not_4_out, R0);
  not not_5 (not_5_out, R1);
  not not_6 (not_6_out, R0);
  not not_7 (not_7_out, R1);
  and and_1 (and_1_out, not_1_out, R1);
  and and_2 (and_2_out, not_2_out, R3, not_3_out);
  and and_3 (and_3_out, not_4_out, R2, not_5_out);
  and and_4 (and_4_out, not_6_out, R3, not_7_out);
  or or_1 (G0, and_1_out, and_2_out);
  or or_2 (G1, and_3_out, and_4_out);
endmodule
