// Logisim project ex07.circ as structural Verilog: 1 circuit, main circuit main
module main (
  input  N3,
  input  N2,
  input  N1,
  input  N0,
  output PRIME
);

  wire and_1_out, and_2_out, and_3_out, and_4_out, not_1_out, not_2_out, not_3_out, not_4_out;

  not not_1 (not_1_out, N3);
  not not_2 (not_2_out, N2);
  not not_3 (not_3_out, N3);
  not not_4 (not_4_out, N2);
  and and_1 (and_1_out, not_1_out, N1);
  and and_2 (and_2_out, not_2_out, N1, N0);
  and and_3 (and_3_out, not_3_out, N2, N0);
  and and_4 (and_4_out, N3, not_4_out, N0);
  or or_1 (PRIME, and_1_out, and_2_out, and_3_out, and_4_out);
endmodule
