// Logisim project ex08.circ as structural Verilog: 1 circuit, main circuit main
module main (
  input  C,
  input  N,
  input  S,
  input  L,
  input  O,
  output EDGE
);

  wire and_1_out, and_2_out, and_3_out, and_4_out, and_5_out, and_6_out, and_7_out, and_8_out, nand_1_out,
       nand_2_out, nand_3_out, nand_4_out, not_1_out, not_2_out, not_3_out, not_4_out, not_5_out, not_6_out,
       not_7_out, not_8_out, not_9_out, not_10_out, not_11_out, not_12_out;

  not not_1 (not_1_out, C);
  not not_2 (not_2_out, C);
  not not_3 (not_3_out, C);
  not not_4 (not_4_out, C);
  nand nand_1 (nand_1_out, C, N);
  not not_5 (not_5_out, S);
  not not_6 (not_6_out, O);
  nand nand_2 (nand_2_out, C, N);
  not not_7 (not_7_out, S);
  not not_8 (not_8_out, O);
  nand nand_3 (nand_3_out, C, N);
  not not_9 (not_9_out, L);
  not not_10 (not_10_out, O);
  nand nand_4 (nand_4_out, C, S);
  not not_11 (not_11_out, L);
  not not_12 (not_12_out, O);
  and and_1 (and_1_out, not_1_out, N, S, L);
  and and_2 (and_2_out, not_2_out, N, S, O);
  and and_3 (and_3_out, not_3_out, N, L, O);
  and and_4 (and_4_out, not_4_out, S, L, O);
  and and_5 (and_5_out, nand_1_out, not_5_out, not_6_out);
  and and_6 (and_6_out, nand_2_out, not_7_out, not_8_out);
  and and_7 (and_7_out, nand_3_out, not_9_out, not_10_out);
  and and_8 (and_8_out, nand_4_out, not_11_out, not_12_out);
  or or_1 (EDGE, and_1_out, and_2_out, and_3_out, and_4_out, and_5_out, and_6_out, and_7_out, and_8_out);
endmodule
