// Logisim project ex01.circ as structural Verilog: 1 circuit, main circuit main
module main (
  input  S0,
  input  X,
  input  Y,
  output OUT
);

  wire and_1_out, and_2_out, not_1_out;

  not not_1 (not_1_out, S0);
  and and_1 (and_1_out, S0, X);
  and and_2 (and_2_out, not_1_out, Y);
  or or_1 (OUT, and_1_out, and_2_out);

  // Notes on the sheet:
  //   . 
  //   B. Este circuito é o Multiplexador 2:1
endmodule
