// Logisim project ex02.circ as structural Verilog: 1 circuit, main circuit main
module main (
  input  SEL,
  output A,
  output B
);

  wire not_1_out;

  not not_1 (not_1_out, SEL);
  and and_1 (A, 1'b1, SEL);
  and and_2 (B, not_1_out, 1'b1);

  // Notes on the sheet:
  //   enquanto o DEMUX direciona uma única entrada para uma entre várias saídas.
  //   B. Este é o demultiplexador 1:2. A diferença é que o MUX seleciona uma entre várias entrada para uma saída, 
endmodule
