// Logisim project ex04.circ as structural Verilog: 1 circuit, main circuit main
module main (
  input  S0,
  input  S1,
  input  U,
  input  T,
  input  L,
  input  P,
  output ADC
);

  wire and_1_out, and_2_out, and_3_out, and_4_out, not_1_out, not_2_out, not_3_out, not_4_out;

  not not_1 (not_1_out, S0);
  and and_1 (and_1_out, U, not_1_out, not_2_out);
  not not_2 (not_2_out, S1);
  and and_2 (and_2_out, T, S1, not_3_out);
  not not_3 (not_3_out, S0);
  and and_3 (and_3_out, L, not_4_out, S0);
  not not_4 (not_4_out, S1);
  and and_4 (and_4_out, P, S0, S1);
  or or_1 (ADC, and_1_out, and_2_out, and_3_out, and_4_out);

  // Notes on the sheet:
  //   B. A taxa individual de cada sensor cai para menos de 1/4 da taxa original,
  //   pois o processador agora precisa dividir o tempo entre os quatro,
  //   além de gastar tempo esperando o sinal establiziar após cada troca
endmodule
