// Logisim project ex05.circ as structural Verilog: 1 circuit, main circuit main
module main (
  input  C1,
  input  C0,
  input  AND,
  input  OR,
  input  ADD,
  input  SUB,
  output Y
);

  wire and_1_out, and_2_out, and_3_out, and_4_out, not_1_out, not_2_out, not_3_out, not_4_out;

  not not_1 (not_1_out, C1);
  not not_2 (not_2_out, C0);
  not not_3 (not_3_out, C1);
  not not_4 (not_4_out, C0);
  and and_1 (and_1_out, AND, not_1_out, not_2_out);
  and and_2 (and_2_out, OR, not_3_out, C0);
  and and_3 (and_3_out, ADD, C1, not_4_out);
  and and_4 (and_4_out, SUB, C1, C0);
  or or_1 (Y, and_1_out, and_2_out, and_3_out, and_4_out);

  // Notes on the sheet:
  //   C. O tempo de calcular todos e depois apenas "escolher" o resultado com o MUX
  //   é menor do que esperar para decidir qual conta fazer e só entao iniciar o cálculo
endmodule
