// Logisim project ex07.circ as structural Verilog: 1 circuit, main circuit main
module main (
  input  S0,
  input  S1,
  input  S2,
  input  R0,
  input  R1,
  input  R2,
  input  R3,
  input  R4,
  input  R5,
  input  R6,
  input  R7,
  output OUT
);

  wire and_1_out, and_2_out, and_3_out, and_4_out, and_5_out, and_6_out, and_7_out, and_8_out, not_1_out,
       not_2_out, not_3_out, not_4_out, not_5_out, not_6_out, not_7_out, not_8_out, not_9_out, not_10_out,
       not_11_out, not_12_out;

  not not_1 (not_1_out, S2);
  not not_2 (not_2_out, S1);
  not not_3 (not_3_out, S0);
  not not_4 (not_4_out, S1);
  not not_5 (not_5_out, S0);
  not not_6 (not_6_out, S2);
  not not_7 (not_7_out, S0);
  not not_8 (not_8_out, S0);
  not not_9 (not_9_out, S2);
  not not_10 (not_10_out, S1);
  not not_11 (not_11_out, S1);
  not not_12 (not_12_out, S2);
  and and_1 (and_1_out, R0, not_1_out, not_2_out, not_3_out);
  and and_2 (and_2_out, R1, S2, not_4_out, not_5_out);
  and and_3 (and_3_out, R2, not_6_out, S1, not_7_out);
  and and_4 (and_4_out, R3, S2, S1, not_8_out);
  and and_5 (and_5_out, R4, not_9_out, not_10_out, S0);
  and and_6 (and_6_out, R5, S2, not_11_out, S0);
  and and_7 (and_7_out, R6, not_12_out, S1, S0);
  and and_8 (and_8_out, R7, S2, S1, S0);
  or or_1 (OUT, and_1_out, and_2_out, and_3_out, and_4_out, and_5_out, and_6_out, and_7_out, and_8_out);
endmodule
