// Logisim project ex01.circ as structural Verilog: 1 circuit, main circuit main
module main (
  input  A,
  input  B,
  input  A_2,
  output S,
  output C
);

  and and_1 (C, A, B);
  xor xor_1 (S, A, B);

  // Notes on the sheet:
  //   A. A porta lógica XOR
  //   B. A porta AND
  //   C. Ele é usado exclusivamente na soma do bit menos significativo (o bit zero da direita),
  //   pois é a única posição que não precisa receber um "vai-um" (carry-in) de uma etapa anterior.
endmodule
