// Logisim project ex02.circ as structural Verilog: 1 circuit, main circuit main
module main (
  input  A0,
  input  A1,
  input  B0,
  input  B1,
  output S0,
  output S1
);

  xor xor_1 (S0, A0, B0);
  xor xor_2 (S1, A1, B1);

  // Notes on the sheet:
  //   O Half Adder não possui um pino de entrada para o Carry (Cin).
  //   o próximo estágio (A1​ e B1​) não tem por onde receber esse carry.
  //   Quando você soma os bits menos significativos (A0​ e B0​) e a soma resulta em um "vai-um" (Cout = 1),
  //   Assim, a propagação do carry é interrompida, resultando em contas erradas sempre que o bit anterior estourar a capacidade.
endmodule
