// Logisim project ex03.circ as structural Verilog: 1 circuit, main circuit main
module main (
  input  A,
  input  B,
  input  Cin,
  output S,
  output Cout
);

  wire and_1_out, and_2_out, xor_1_out, xor_2_out;

  xor xor_1 (xor_1_out, A, B);
  and and_1 (and_1_out, A, B);
  xor xor_2 (xor_2_out, A, B);
  xor xor_3 (S, xor_1_out, Cin);
  and and_2 (and_2_out, Cin, xor_2_out);
  or or_1 (Cout, and_1_out, and_2_out);

  // Notes on the sheet:
  //   de múltiplos bits de qualquer tamanho dentro do processador.
  //   A presença do pino Cin e do pino Cout permite que você conecte vários Full Adders em cascata.
  //   O Cout de um bit vira o Cin do próximo bit, permitindo a construção de somadores
endmodule
