// Logisim project ex04.circ as structural Verilog: 1 circuit, main circuit main
module main (
  input  A0,
  input  B0,
  input  Cin,
  input  A1,
  input  B1,
  input  A2,
  input  B2,
  input  A3,
  input  B3,
  output S,
  output Cout,
  output S_2,
  output Cout_2,
  output S_3,
  output Cout_3,
  output S_4,
  output Cout_4
);

  wire and_1_out, and_2_out, and_3_out, and_4_out, and_5_out, and_6_out, and_7_out, and_8_out, xor_1_out,
       xor_2_out, xor_3_out, xor_4_out, xor_5_out, xor_6_out, xor_7_out, xor_8_out;

  xor xor_1 (xor_1_out, A0, B0);
  and and_1 (and_1_out, A0, B0);
  xor xor_2 (xor_2_out, A0, B0);
  xor xor_3 (xor_3_out, A1, B1);
  and and_2 (and_2_out, A1, B1);
  xor xor_4 (xor_4_out, A1, B1);
  xor xor_5 (xor_5_out, A2, B2);
  and and_3 (and_3_out, A2, B2);
  xor xor_6 (xor_6_out, A2, B2);
  xor xor_7 (xor_7_out, A3, B3);
  and and_4 (and_4_out, A3, B3);
  xor xor_8 (xor_8_out, A3, B3);
  xor xor_9 (S, xor_1_out, Cin);
  xor xor_10 (S_2, xor_3_out, Cout);
  xor xor_11 (S_3, xor_5_out, Cout_2);
  xor xor_12 (S_4, xor_7_out, Cout_3);
  and and_5 (and_5_out, Cin, xor_2_out);
  and and_6 (and_6_out, Cout, xor_4_out);
  and and_7 (and_7_out, Cout_2, xor_6_out);
  and and_8 (and_8_out, Cout_3, xor_8_out);
  or or_1 (Cout, and_1_out, and_5_out);
  or or_2 (Cout_2, and_2_out, and_6_out);
  or or_3 (Cout_3, and_3_out, and_7_out);
  or or_4 (Cout_4, and_4_out, and_8_out);

  // Notes on the sheet:
  //   A. São necessários exatamente 4 Full Adders em série.
  //   B. O tempo de propagação aumenta de forma linear.
  //   O resultado do bit mais significativo (S3​) só fica pronto depois que o carry "viajar" fisicamente pelos somadores dos bits 0, 1 e 2.
endmodule
