// Logisim project ex06.circ as structural Verilog: 1 circuit, main circuit main
module main (
  input  B0,
  input  A0,
  input  B1,
  input  A1,
  input  B2,
  input  A2,
  input  B3,
  input  A3,
  output S,
  output Cout,
  output S_2,
  output Cout_2,
  output S_3,
  output Cout_3,
  output S_4,
  output Cout_4
);

  wire and_1_out, and_2_out, and_3_out, and_4_out, and_5_out, and_6_out, and_7_out, and_8_out, not_1_out,
       not_2_out, not_3_out, not_4_out, xor_1_out, xor_2_out, xor_3_out, xor_4_out, xor_5_out, xor_6_out,
       xor_7_out, xor_8_out;

  not not_1 (not_1_out, B0);
  not not_2 (not_2_out, B1);
  not not_3 (not_3_out, B2);
  not not_4 (not_4_out, B3);
  xor xor_1 (xor_1_out, A0, not_1_out);
  and and_1 (and_1_out, A0, not_1_out);
  xor xor_2 (xor_2_out, A0, not_1_out);
  xor xor_3 (xor_3_out, A1, not_2_out);
  and and_2 (and_2_out, A1, not_2_out);
  xor xor_4 (xor_4_out, A1, not_2_out);
  xor xor_5 (xor_5_out, A2, not_3_out);
  and and_3 (and_3_out, A2, not_3_out);
  xor xor_6 (xor_6_out, A2, not_3_out);
  xor xor_7 (xor_7_out, A3, not_4_out);
  and and_4 (and_4_out, A3, not_4_out);
  xor xor_8 (xor_8_out, A3, not_4_out);
  xor xor_9 (S, xor_1_out, 1'b1);
  xor xor_10 (S_2, xor_3_out, Cout);
  xor xor_11 (S_3, xor_5_out, Cout_2);
  xor xor_12 (S_4, xor_7_out, Cout_3);
  and and_5 (and_5_out, 1'b1, xor_2_out);
  and and_6 (and_6_out, Cout, xor_4_out);
  and and_7 (and_7_out, Cout_2, xor_6_out);
  and and_8 (and_8_out, Cout_3, xor_8_out);
  or or_1 (Cout, and_1_out, and_5_out);
  or or_2 (Cout_2, and_2_out, and_6_out);
  or or_3 (Cout_3, and_3_out, and_7_out);
  or or_4 (Cout_4, and_4_out, and_8_out);

  // Notes on the sheet:
  //   A. O resultado é processado e gerado nativamente já no formato binário de Complemento de 2.
  //   C. Em operações de subtração em complemento de 2, o Cout invertido funciona como a flag de "Borrow" (Empréstimo).
  //   B. O bit mais significativo (MSB, no caso D3​) assume o valor 1, o que funciona como o sinal indicando que o número é negativo.
  //   Se o carry final for 1, o resultado é positivo e não houve empréstimo. Se for 0, o resultado é negativo (precisou de empréstimo virtual).
endmodule
