// Logisim project ex07.circ as structural Verilog: 1 circuit, main circuit main
module main (
  input  A0,
  input  B0,
  input  A0_2,
  input  B0_2,
  input  Cin,
  input  A4,
  input  B4,
  input  A0_3,
  input  B0_3,
  input  A1,
  input  B1,
  input  A1_2,
  input  B1_2,
  input  A1_3,
  input  B1_3,
  input  A1_4,
  input  B1_4,
  input  A2,
  input  B2,
  input  A2_2,
  input  B2_2,
  input  A2_3,
  input  B2_3,
  input  A2_4,
  input  B2_4,
  input  A3,
  input  B3,
  input  A3_2,
  input  B3_2,
  input  A3_3,
  input  B3_3,
  input  A3_4,
  input  B3_4,
  output S,
  output S_2,
  output S_3,
  output S_4,
  output Cout,
  output Cout_2,
  output Cout_3,
  output Cout_4,
  output S_5,
  output S_6,
  output S_7,
  output S_8,
  output Cout_5,
  output Cout_6,
  output Cout_7,
  output Cout_8,
  output S_9,
  output S_10,
  output S_11,
  output S_12,
  output Cout_9,
  output Cout_10,
  output Cout_11,
  output Cout_12,
  output S_13,
  output S_14,
  output S_15,
  output S_16,
  output Cout_13,
  output Cout_14,
  output Cout_15,
  output Cout_16
);

  wire and_1_out, and_2_out, and_3_out, and_4_out, and_5_out, and_6_out, and_7_out, and_8_out, and_9_out,
       and_10_out, and_11_out, and_12_out, and_13_out, and_14_out, and_15_out, and_16_out, and_17_out,
       and_18_out, and_19_out, and_20_out, and_21_out, and_22_out, and_23_out, and_24_out, and_25_out,
       and_26_out, and_27_out, and_28_out, and_29_out, and_30_out, and_31_out, and_32_out, xor_1_out,
       xor_2_out, xor_3_out, xor_4_out, xor_5_out, xor_6_out, xor_7_out, xor_8_out, xor_13_out, xor_14_out,
       xor_15_out, xor_16_out, xor_17_out, xor_18_out, xor_19_out, xor_20_out, xor_25_out, xor_26_out,
       xor_27_out, xor_28_out, xor_29_out, xor_30_out, xor_31_out, xor_32_out, xor_37_out, xor_38_out,
       xor_39_out, xor_40_out, xor_41_out, xor_42_out, xor_43_out, xor_44_out;

  xor xor_1 (xor_1_out, A0_2, B0_2);
  and and_1 (and_1_out, A0_2, B0_2);
  xor xor_2 (xor_2_out, A0_2, B0_2);
  xor xor_3 (xor_3_out, A1_2, B1_2);
  and and_2 (and_2_out, A1_2, B1_2);
  xor xor_4 (xor_4_out, A1_2, B1_2);
  xor xor_5 (xor_5_out, A2_2, B2_2);
  and and_3 (and_3_out, A2_2, B2_2);
  xor xor_6 (xor_6_out, A2_2, B2_2);
  xor xor_7 (xor_7_out, A3_2, B3_2);
  and and_4 (and_4_out, A3_2, B3_2);
  xor xor_8 (xor_8_out, A3_2, B3_2);
  xor xor_9 (S_2, xor_1_out, Cin);
  xor xor_10 (S_6, xor_3_out, Cout_2);
  xor xor_11 (S_10, xor_5_out, Cout_6);
  xor xor_12 (S_14, xor_7_out, Cout_10);
  and and_5 (and_5_out, Cin, xor_2_out);
  and and_6 (and_6_out, Cout_2, xor_4_out);
  and and_7 (and_7_out, Cout_6, xor_6_out);
  and and_8 (and_8_out, Cout_10, xor_8_out);
  or or_1 (Cout_2, and_1_out, and_5_out);
  or or_2 (Cout_6, and_2_out, and_6_out);
  or or_3 (Cout_10, and_3_out, and_7_out);
  or or_4 (Cout_14, and_4_out, and_8_out);
  xor xor_13 (xor_13_out, A4, B4);
  and and_9 (and_9_out, A4, B4);
  xor xor_14 (xor_14_out, A4, B4);
  xor xor_15 (xor_15_out, A1_3, B1_3);
  and and_10 (and_10_out, A1_3, B1_3);
  xor xor_16 (xor_16_out, A1_3, B1_3);
  xor xor_17 (xor_17_out, A2_3, B2_3);
  and and_11 (and_11_out, A2_3, B2_3);
  xor xor_18 (xor_18_out, A2_3, B2_3);
  xor xor_19 (xor_19_out, A3_3, B3_3);
  and and_12 (and_12_out, A3_3, B3_3);
  xor xor_20 (xor_20_out, A3_3, B3_3);
  xor xor_21 (S_3, xor_13_out, Cout_14);
  and and_13 (and_13_out, Cout_14, xor_14_out);
  xor xor_22 (S_7, xor_15_out, Cout_3);
  and and_14 (and_14_out, Cout_3, xor_16_out);
  xor xor_23 (S_11, xor_17_out, Cout_7);
  and and_15 (and_15_out, Cout_7, xor_18_out);
  xor xor_24 (S_15, xor_19_out, Cout_11);
  and and_16 (and_16_out, Cout_11, xor_20_out);
  or or_5 (Cout_3, and_9_out, and_13_out);
  or or_6 (Cout_7, and_10_out, and_14_out);
  or or_7 (Cout_11, and_11_out, and_15_out);
  or or_8 (Cout_15, and_12_out, and_16_out);
  xor xor_25 (xor_25_out, A0, B0);
  and and_17 (and_17_out, A0, B0);
  xor xor_26 (xor_26_out, A0, B0);
  xor xor_27 (xor_27_out, A1, B1);
  and and_18 (and_18_out, A1, B1);
  xor xor_28 (xor_28_out, A1, B1);
  xor xor_29 (xor_29_out, A2, B2);
  and and_19 (and_19_out, A2, B2);
  xor xor_30 (xor_30_out, A2, B2);
  xor xor_31 (xor_31_out, A3, B3);
  and and_20 (and_20_out, A3, B3);
  xor xor_32 (xor_32_out, A3, B3);
  xor xor_33 (S, xor_25_out, Cout_15);
  and and_21 (and_21_out, Cout_15, xor_26_out);
  xor xor_34 (S_5, xor_27_out, Cout);
  and and_22 (and_22_out, Cout, xor_28_out);
  xor xor_35 (S_9, xor_29_out, Cout_5);
  and and_23 (and_23_out, Cout_5, xor_30_out);
  xor xor_36 (S_13, xor_31_out, Cout_9);
  and and_24 (and_24_out, Cout_9, xor_32_out);
  or or_9 (Cout, and_17_out, and_21_out);
  or or_10 (Cout_5, and_18_out, and_22_out);
  or or_11 (Cout_9, and_19_out, and_23_out);
  or or_12 (Cout_13, and_20_out, and_24_out);
  xor xor_37 (xor_37_out, A0_3, B0_3);
  and and_25 (and_25_out, A0_3, B0_3);
  xor xor_38 (xor_38_out, A0_3, B0_3);
  xor xor_39 (xor_39_out, A1_4, B1_4);
  and and_26 (and_26_out, A1_4, B1_4);
  xor xor_40 (xor_40_out, A1_4, B1_4);
  xor xor_41 (xor_41_out, A2_4, B2_4);
  and and_27 (and_27_out, A2_4, B2_4);
  xor xor_42 (xor_42_out, A2_4, B2_4);
  xor xor_43 (xor_43_out, A3_4, B3_4);
  and and_28 (and_28_out, A3_4, B3_4);
  xor xor_44 (xor_44_out, A3_4, B3_4);
  xor xor_45 (S_4, xor_37_out, Cout_13);
  and and_29 (and_29_out, Cout_13, xor_38_out);
  xor xor_46 (S_8, xor_39_out, Cout_4);
  and and_30 (and_30_out, Cout_4, xor_40_out);
  xor xor_47 (S_12, xor_41_out, Cout_8);
  and and_31 (and_31_out, Cout_8, xor_42_out);
  xor xor_48 (S_16, xor_43_out, Cout_12);
  and and_32 (and_32_out, Cout_12, xor_44_out);
  or or_13 (Cout_4, and_25_out, and_29_out);
  or or_14 (Cout_8, and_26_out, and_30_out);
  or or_15 (Cout_12, and_27_out, and_31_out);
  or or_16 (Cout_16, and_28_out, and_32_out);

  // Notes on the sheet:
  //   Em processadores reais, esse circuito gigante é a base que executa as instruções assembly de adição, calcula endereços de ponteiros de memória (somando a base com o offset) e gerencia contadores de loops de 16 bits nativos da arquitetura.
endmodule
