// Logisim project ex09.circ as structural Verilog: 1 circuit, main circuit main
module main (
  input  A0,
  input  B0,
  input  A0_2,
  input  B0_2,
  input  Cin,
  input  A4,
  input  B4,
  input  A0_3,
  input  B0_3,
  input  A0_4,
  input  B0_4,
  input  A0_5,
  input  B0_5,
  input  A4_2,
  input  B4_2,
  input  A0_6,
  input  B0_6,
  input  A1,
  input  B1,
  input  A1_2,
  input  B1_2,
  input  A1_3,
  input  B1_3,
  input  A1_4,
  input  B1_4,
  input  A1_5,
  input  B1_5,
  input  A1_6,
  input  B1_6,
  input  A1_7,
  input  B1_7,
  input  A1_8,
  input  B1_8,
  input  A2,
  input  B2,
  input  A2_2,
  input  B2_2,
  input  A2_3,
  input  B2_3,
  input  A2_4,
  input  B2_4,
  input  A2_5,
  input  B2_5,
  input  A2_6,
  input  B2_6,
  input  A2_7,
  input  B2_7,
  input  A2_8,
  input  B2_8,
  input  A3,
  input  B3,
  input  A3_2,
  input  B3_2,
  input  A3_3,
  input  B3_3,
  input  A3_4,
  input  B3_4,
  input  A3_5,
  input  B3_5,
  input  A3_6,
  input  B3_6,
  input  A3_7,
  input  B3_7,
  input  A3_8,
  input  B3_8,
  output S,
  output S_2,
  output S_3,
  output S_4,
  output S_5,
  output S_6,
  output S_7,
  output S_8,
  output Cout,
  output Cout_2,
  output Cout_3,
  output Cout_4,
  output Cout_5,
  output Cout_6,
  output Cout_7,
  output Cout_8,
  output S_9,
  output S_10,
  output S_11,
  output S_12,
  output S_13,
  output S_14,
  output S_15,
  output S_16,
  output Cout_9,
  output Cout_10,
  output Cout_11,
  output Cout_12,
  output Cout_13,
  output Cout_14,
  output Cout_15,
  output Cout_16,
  output S_17,
  output S_18,
  output S_19,
  output S_20,
  output S_21,
  output S_22,
  output S_23,
  output S_24,
  output Cout_17,
  output Cout_18,
  output Cout_19,
  output Cout_20,
  output Cout_21,
  output Cout_22,
  output Cout_23,
  output Cout_24,
  output S_25,
  output S_26,
  output S_27,
  output S_28,
  output S_29,
  output S_30,
  output S_31,
  output S_32,
  output Cout_25,
  output Cout_26,
  output Cout_27,
  output Cout_28,
  output Cout_29,
  output Cout_30,
  output Cout_31,
  output Cout_32
);

  wire and_1_out, and_2_out, and_3_out, and_4_out, and_5_out, and_6_out, and_7_out, and_8_out, and_9_out,
       and_10_out, and_11_out, and_12_out, and_13_out, and_14_out, and_15_out, and_16_out, and_17_out,
       and_18_out, and_19_out, and_20_out, and_21_out, and_22_out, and_23_out, and_24_out, and_25_out,
       and_26_out, and_27_out, and_28_out, and_29_out, and_30_out, and_31_out, and_32_out, and_33_out,
       and_34_out, and_35_out, and_36_out, and_37_out, and_38_out, and_39_out, and_40_out, and_41_out,
       and_42_out, and_43_out, and_44_out, and_45_out, and_46_out, and_47_out, and_48_out, and_49_out,
       and_50_out, and_51_out, and_52_out, and_53_out, and_54_out, and_55_out, and_56_out, and_57_out,
       and_58_out, and_59_out, and_60_out, and_61_out, and_62_out, and_63_out, and_64_out, xor_1_out,
       xor_2_out, xor_3_out, xor_4_out, xor_5_out, xor_6_out, xor_7_out, xor_8_out, xor_13_out, xor_14_out,
       xor_15_out, xor_16_out, xor_17_out, xor_18_out, xor_19_out, xor_20_out, xor_25_out, xor_26_out,
       xor_27_out, xor_28_out, xor_29_out, xor_30_out, xor_31_out, xor_32_out, xor_37_out, xor_38_out,
       xor_39_out, xor_40_out, xor_41_out, xor_42_out, xor_43_out, xor_44_out, xor_49_out, xor_50_out,
       xor_51_out, xor_52_out, xor_53_out, xor_54_out, xor_55_out, xor_56_out, xor_61_out, xor_62_out,
       xor_63_out, xor_64_out, xor_65_out, xor_66_out, xor_67_out, xor_68_out, xor_73_out, xor_74_out,
       xor_75_out, xor_76_out, xor_77_out, xor_78_out, xor_79_out, xor_80_out, xor_85_out, xor_86_out,
       xor_87_out, xor_88_out, xor_89_out, xor_90_out, xor_91_out, xor_92_out;

  xor xor_1 (xor_1_out, A0_2, B0_2);
  and and_1 (and_1_out, A0_2, B0_2);
  xor xor_2 (xor_2_out, A0_2, B0_2);
  xor xor_3 (xor_3_out, A1_2, B1_2);
  and and_2 (and_2_out, A1_2, B1_2);
  xor xor_4 (xor_4_out, A1_2, B1_2);
  xor xor_5 (xor_5_out, A2_2, B2_2);
  and and_3 (and_3_out, A2_2, B2_2);
  xor xor_6 (xor_6_out, A2_2, B2_2);
  xor xor_7 (xor_7_out, A3_2, B3_2);
  and and_4 (and_4_out, A3_2, B3_2);
  xor xor_8 (xor_8_out, A3_2, B3_2);
  xor xor_9 (S_2, xor_1_out, Cin);
  xor xor_10 (S_10, xor_3_out, Cout_2);
  xor xor_11 (S_18, xor_5_out, Cout_10);
  xor xor_12 (S_26, xor_7_out, Cout_18);
  and and_5 (and_5_out, Cin, xor_2_out);
  and and_6 (and_6_out, Cout_2, xor_4_out);
  and and_7 (and_7_out, Cout_10, xor_6_out);
  and and_8 (and_8_out, Cout_18, xor_8_out);
  or or_1 (Cout_2, and_1_out, and_5_out);
  or or_2 (Cout_10, and_2_out, and_6_out);
  or or_3 (Cout_18, and_3_out, and_7_out);
  or or_4 (Cout_26, and_4_out, and_8_out);
  xor xor_13 (xor_13_out, A4, B4);
  and and_9 (and_9_out, A4, B4);
  xor xor_14 (xor_14_out, A4, B4);
  xor xor_15 (xor_15_out, A1_3, B1_3);
  and and_10 (and_10_out, A1_3, B1_3);
  xor xor_16 (xor_16_out, A1_3, B1_3);
  xor xor_17 (xor_17_out, A2_3, B2_3);
  and and_11 (and_11_out, A2_3, B2_3);
  xor xor_18 (xor_18_out, A2_3, B2_3);
  xor xor_19 (xor_19_out, A3_3, B3_3);
  and and_12 (and_12_out, A3_3, B3_3);
  xor xor_20 (xor_20_out, A3_3, B3_3);
  xor xor_21 (S_3, xor_13_out, Cout_26);
  and and_13 (and_13_out, Cout_26, xor_14_out);
  xor xor_22 (S_11, xor_15_out, Cout_3);
  and and_14 (and_14_out, Cout_3, xor_16_out);
  xor xor_23 (S_19, xor_17_out, Cout_11);
  and and_15 (and_15_out, Cout_11, xor_18_out);
  xor xor_24 (S_27, xor_19_out, Cout_19);
  and and_16 (and_16_out, Cout_19, xor_20_out);
  or or_5 (Cout_3, and_9_out, and_13_out);
  or or_6 (Cout_11, and_10_out, and_14_out);
  or or_7 (Cout_19, and_11_out, and_15_out);
  or or_8 (Cout_27, and_12_out, and_16_out);
  xor xor_25 (xor_25_out, A0, B0);
  and and_17 (and_17_out, A0, B0);
  xor xor_26 (xor_26_out, A0, B0);
  xor xor_27 (xor_27_out, A1, B1);
  and and_18 (and_18_out, A1, B1);
  xor xor_28 (xor_28_out, A1, B1);
  xor xor_29 (xor_29_out, A2, B2);
  and and_19 (and_19_out, A2, B2);
  xor xor_30 (xor_30_out, A2, B2);
  xor xor_31 (xor_31_out, A3, B3);
  and and_20 (and_20_out, A3, B3);
  xor xor_32 (xor_32_out, A3, B3);
  xor xor_33 (S, xor_25_out, Cout_27);
  and and_21 (and_21_out, Cout_27, xor_26_out);
  xor xor_34 (S_9, xor_27_out, Cout);
  and and_22 (and_22_out, Cout, xor_28_out);
  xor xor_35 (S_17, xor_29_out, Cout_9);
  and and_23 (and_23_out, Cout_9, xor_30_out);
  xor xor_36 (S_25, xor_31_out, Cout_17);
  and and_24 (and_24_out, Cout_17, xor_32_out);
  or or_9 (Cout, and_17_out, and_21_out);
  or or_10 (Cout_9, and_18_out, and_22_out);
  or or_11 (Cout_17, and_19_out, and_23_out);
  or or_12 (Cout_25, and_20_out, and_24_out);
  xor xor_37 (xor_37_out, A0_3, B0_3);
  and and_25 (and_25_out, A0_3, B0_3);
  xor xor_38 (xor_38_out, A0_3, B0_3);
  xor xor_39 (xor_39_out, A1_4, B1_4);
  and and_26 (and_26_out, A1_4, B1_4);
  xor xor_40 (xor_40_out, A1_4, B1_4);
  xor xor_41 (xor_41_out, A2_4, B2_4);
  and and_27 (and_27_out, A2_4, B2_4);
  xor xor_42 (xor_42_out, A2_4, B2_4);
  xor xor_43 (xor_43_out, A3_4, B3_4);
  and and_28 (and_28_out, A3_4, B3_4);
  xor xor_44 (xor_44_out, A3_4, B3_4);
  xor xor_45 (S_4, xor_37_out, Cout_25);
  and and_29 (and_29_out, Cout_25, xor_38_out);
  xor xor_46 (S_12, xor_39_out, Cout_4);
  and and_30 (and_30_out, Cout_4, xor_40_out);
  xor xor_47 (S_20, xor_41_out, Cout_12);
  and and_31 (and_31_out, Cout_12, xor_42_out);
  xor xor_48 (S_28, xor_43_out, Cout_20);
  and and_32 (and_32_out, Cout_20, xor_44_out);
  or or_13 (Cout_4, and_25_out, and_29_out);
  or or_14 (Cout_12, and_26_out, and_30_out);
  or or_15 (Cout_20, and_27_out, and_31_out);
  or or_16 (Cout_28, and_28_out, and_32_out);
  and and_33 (and_33_out, A0_5, B0_5);
  and and_34 (and_34_out, A1_6, B1_6);
  and and_35 (and_35_out, A2_6, B2_6);
  and and_36 (and_36_out, A3_6, B3_6);
  xor xor_49 (xor_49_out, A0_5, B0_5);
  xor xor_50 (xor_50_out, A0_5, B0_5);
  xor xor_51 (xor_51_out, A1_6, B1_6);
  xor xor_52 (xor_52_out, A1_6, B1_6);
  xor xor_53 (xor_53_out, A2_6, B2_6);
  xor xor_54 (xor_54_out, A2_6, B2_6);
  xor xor_55 (xor_55_out, A3_6, B3_6);
  xor xor_56 (xor_56_out, A3_6, B3_6);
  xor xor_57 (S_6, xor_49_out, Cout_28);
  and and_37 (and_37_out, Cout_28, xor_50_out);
  xor xor_58 (S_14, xor_51_out, Cout_6);
  and and_38 (and_38_out, Cout_6, xor_52_out);
  xor xor_59 (S_22, xor_53_out, Cout_14);
  and and_39 (and_39_out, Cout_14, xor_54_out);
  xor xor_60 (S_30, xor_55_out, Cout_22);
  and and_40 (and_40_out, Cout_22, xor_56_out);
  or or_17 (Cout_6, and_33_out, and_37_out);
  or or_18 (Cout_14, and_34_out, and_38_out);
  or or_19 (Cout_22, and_35_out, and_39_out);
  or or_20 (Cout_30, and_36_out, and_40_out);
  xor xor_61 (xor_61_out, A4_2, B4_2);
  and and_41 (and_41_out, A4_2, B4_2);
  xor xor_62 (xor_62_out, A4_2, B4_2);
  xor xor_63 (xor_63_out, A1_7, B1_7);
  and and_42 (and_42_out, A1_7, B1_7);
  xor xor_64 (xor_64_out, A1_7, B1_7);
  xor xor_65 (xor_65_out, A2_7, B2_7);
  and and_43 (and_43_out, A2_7, B2_7);
  xor xor_66 (xor_66_out, A2_7, B2_7);
  xor xor_67 (xor_67_out, A3_7, B3_7);
  and and_44 (and_44_out, A3_7, B3_7);
  xor xor_68 (xor_68_out, A3_7, B3_7);
  xor xor_69 (S_7, xor_61_out, Cout_30);
  xor xor_70 (S_15, xor_63_out, Cout_7);
  xor xor_71 (S_23, xor_65_out, Cout_15);
  xor xor_72 (S_31, xor_67_out, Cout_23);
  and and_45 (and_45_out, Cout_30, xor_62_out);
  and and_46 (and_46_out, Cout_7, xor_64_out);
  and and_47 (and_47_out, Cout_15, xor_66_out);
  and and_48 (and_48_out, Cout_23, xor_68_out);
  or or_21 (Cout_7, and_41_out, and_45_out);
  or or_22 (Cout_15, and_42_out, and_46_out);
  or or_23 (Cout_23, and_43_out, and_47_out);
  or or_24 (Cout_31, and_44_out, and_48_out);
  xor xor_73 (xor_73_out, A0_4, B0_4);
  and and_49 (and_49_out, A0_4, B0_4);
  xor xor_74 (xor_74_out, A0_4, B0_4);
  xor xor_75 (xor_75_out, A1_5, B1_5);
  and and_50 (and_50_out, A1_5, B1_5);
  xor xor_76 (xor_76_out, A1_5, B1_5);
  xor xor_77 (xor_77_out, A2_5, B2_5);
  and and_51 (and_51_out, A2_5, B2_5);
  xor xor_78 (xor_78_out, A2_5, B2_5);
  xor xor_79 (xor_79_out, A3_5, B3_5);
  and and_52 (and_52_out, A3_5, B3_5);
  xor xor_80 (xor_80_out, A3_5, B3_5);
  xor xor_81 (S_5, xor_73_out, Cout_31);
  xor xor_82 (S_13, xor_75_out, Cout_5);
  xor xor_83 (S_21, xor_77_out, Cout_13);
  xor xor_84 (S_29, xor_79_out, Cout_21);
  and and_53 (and_53_out, Cout_31, xor_74_out);
  and and_54 (and_54_out, Cout_5, xor_76_out);
  and and_55 (and_55_out, Cout_13, xor_78_out);
  and and_56 (and_56_out, Cout_21, xor_80_out);
  or or_25 (Cout_5, and_49_out, and_53_out);
  or or_26 (Cout_13, and_50_out, and_54_out);
  or or_27 (Cout_21, and_51_out, and_55_out);
  or or_28 (Cout_29, and_52_out, and_56_out);
  xor xor_85 (xor_85_out, A0_6, B0_6);
  and and_57 (and_57_out, A0_6, B0_6);
  xor xor_86 (xor_86_out, A0_6, B0_6);
  xor xor_87 (xor_87_out, A1_8, B1_8);
  and and_58 (and_58_out, A1_8, B1_8);
  xor xor_88 (xor_88_out, A1_8, B1_8);
  xor xor_89 (xor_89_out, A2_8, B2_8);
  and and_59 (and_59_out, A2_8, B2_8);
  xor xor_90 (xor_90_out, A2_8, B2_8);
  xor xor_91 (xor_91_out, A3_8, B3_8);
  and and_60 (and_60_out, A3_8, B3_8);
  xor xor_92 (xor_92_out, A3_8, B3_8);
  xor xor_93 (S_8, xor_85_out, Cout_29);
  xor xor_94 (S_16, xor_87_out, Cout_8);
  xor xor_95 (S_24, xor_89_out, Cout_16);
  xor xor_96 (S_32, xor_91_out, Cout_24);
  and and_61 (and_61_out, Cout_29, xor_86_out);
  and and_62 (and_62_out, Cout_8, xor_88_out);
  and and_63 (and_63_out, Cout_16, xor_90_out);
  and and_64 (and_64_out, Cout_24, xor_92_out);
  or or_29 (Cout_8, and_57_out, and_61_out);
  or or_30 (Cout_16, and_58_out, and_62_out);
  or or_31 (Cout_24, and_59_out, and_63_out);
  or or_32 (Cout_32, and_60_out, and_64_out);

  // Notes on the sheet:
  //   Para implementar um somador de 32 bits pela técnica Ripple Carry, você encadearia 32 blocos de Full Adders.
endmodule
