// Logisim project ex04.circ as structural Verilog: 1 circuit, main circuit main
module main (
  input  [1:0] in_1,
  input  [3:0] in_2,
  input  in_3,
  output [3:0] out_4
);

  wire clock_1_out;

  Clock clock_1 (.out(clock_1_out));
  RAM #(.addrWidth(2), .dataWidth(4), .bus("separate")) ram_1 (
    .addr(in_1), .din(in_2), .data(out_4), .str(in_3), .sel(1'b1), .clk(clock_1_out), .ld(1'b1), .clr(1'b0));
endmodule
