// Logisim project ex05.circ as structural Verilog: 1 circuit, main circuit main
module main (
  output out_1,
  output out_2,
  output out_3,
  output out_4
);

  wire clock_1_out, Start_out, xor_1_out;

  Clock clock_1 (.out(clock_1_out));
  Button Start (.out(Start_out));
  D_Flip_Flop FF3 (.clk(clock_1_out), .D(xor_1_out), .Q(out_1), .preset(Start_out));  // open: Qn, en, reset
  xor xor_1 (xor_1_out, out_4, out_1);
  D_Flip_Flop FF2 (.clk(clock_1_out), .D(out_1), .Q(out_2), .preset(Start_out));  // open: Qn, en, reset
  D_Flip_Flop FF1 (.clk(clock_1_out), .D(out_2), .Q(out_3), .reset(Start_out));  // open: Qn, preset, en
  D_Flip_Flop FF0 (.clk(clock_1_out), .D(out_3), .Q(out_4), .preset(Start_out));  // open: Qn, en, reset
endmodule
