// Logisim project ex06.circ as structural Verilog: 1 circuit, main circuit main
module main (
  input  reset,
  input  [7:0] seed,
  output [7:0] out_3
);

  wire clock_1_out;
  wire [0:0] xor_1_out;
  wire [7:0] multiplexer_1_out;

  Multiplexer #(.width(8)) multiplexer_1 (
    .in0({out_3[6:0], xor_1_out[0]}), .in1(seed), .out(multiplexer_1_out), .sel(reset));  // open: en
  Clock clock_1 (.out(clock_1_out));
  Register register_1 (.D(multiplexer_1_out), .en(1'b1), .Q(out_3), .clk(clock_1_out));  // open: clr
  ExactlyOne xor_1 (.out(xor_1_out[0]), .in0(out_3[7]), .in1(out_3[5]), .in2(out_3[4]), .in3(out_3[3]));
endmodule
