// Logisim project ex07.circ as structural Verilog: 1 circuit, main circuit main
module main (
  input  Coin,
  input  Select,
  input  Done,
  output Busy,
  output Coffe
);

  wire and_1_out, and_2_out, and_3_out, and_4_out, and_5_out, B_q, clock_1_out, not_1_out, not_2_out,
       not_3_out, or_1_out, or_2_out;

  not not_1 (not_1_out, Busy);
  not not_2 (not_2_out, B_q);
  and and_1 (and_1_out, Select, not_1_out, B_q);
  and and_2 (and_2_out, not_2_out, Busy);
  not not_3 (not_3_out, Select);
  or or_1 (or_1_out, and_1_out, and_2_out);
  Clock clock_1 (.out(clock_1_out));
  and and_3 (and_3_out, not_1_out, B_q, not_3_out);
  D_Flip_Flop A (.clk(clock_1_out), .D(or_1_out), .Q(Busy), .en(1'b1));  // open: Qn, preset, reset
  and and_4 (and_4_out, Coin, not_2_out, not_1_out);
  and and_5 (and_5_out, Done, not_2_out, Busy);
  or or_2 (or_2_out, and_4_out, and_3_out, and_5_out);
  D_Flip_Flop B (.clk(clock_1_out), .D(or_2_out), .Q(B_q), .en(1'b1));  // open: Qn, preset, reset
  and and_6 (Coffe, B_q, Busy);
endmodule
