// Logisim project ex08.circ as structural Verilog: 1 circuit, main circuit main
module main (
  input  enable,
  input  reset,
  input  CLK,
  input  [7:0] limit,
  output interrupt
);

  wire comparator_1_eq;
  wire [7:0] adder_1_out, multiplexer_1_out, register_1_q;

  Register register_1 (.D(multiplexer_1_out), .en(enable), .Q(register_1_q), .clk(CLK), .clr(reset));
  Adder adder_1 (.a(register_1_q), .b(8'h1), .out(adder_1_out));  // open: cin, cout
  Comparator comparator_1 (.a(register_1_q), .b(limit), .eq(comparator_1_eq));  // open: gt, lt
  Multiplexer #(.width(8)) multiplexer_1 (
    .in0(adder_1_out), .in1({8{1'b0}}), .out(multiplexer_1_out), .sel(comparator_1_eq));  // open: en
  and and_1 (interrupt, comparator_1_eq, enable);
endmodule
